// Logisim project ex3.circ as structural Verilog: 1 circuit, main circuit AddMachine
module AddMachine (
  input  clk,
  output [7:0] out_2,
  output [7:0] out_3,
  output [7:0] ADD_OUT,
  output [7:0] REG_OUT
);

  Register register_1 (.D(out_2), .clk(clk), .Q(out_3));  // open: en, clr
  Adder adder_1 (.a(8'h1), .b(out_3), .out(out_2));  // open: cin, cout
endmodule
