// Logisim project ex1.circ as structural Verilog: 1 circuit, main circuit generate_immediate
module generate_immediate (
  input  [31:0] INSTRUCTION,
  output [31:0] IMMEDIATE
);

  assign IMMEDIATE[31:11] = {{20{INSTRUCTION[31]}}, INSTRUCTION[31]};  // Bit_Extender bit_extender_1

  assign IMMEDIATE[10:0] = {INSTRUCTION[30:25], INSTRUCTION[11:7]};

  // Other names for the same wires on the sheet: Tun[31:0] = {IMMEDIATE[31:11], INSTRUCTION[30:25], INSTRUCTION[11:7]}
endmodule
